// Logisim project ALU15.circ as structural Verilog: 1 circuit, main circuit ALU15
module ALU15 (
  input  op,
  input  [14:0] B,
  input  [14:0] A,
  output comp,
  output [14:0] out_5,
  output cout
);

  wire ic_7404_1_p1;
  wire [14:0] xor_1_out, xor_2_out;
  wire [14:14] ic_7408_1_p4, ic_7408_1_p6;

  Comparator #(.width(15), .mode("unsigned")) comparator_1 (.a(A), .b(B), .lt(comp));  // open: gt, eq
  // IC_7404 ic_7404_1: pin names not known; wires that end beside it: ic_7404_1_p1, comp
  // IC_7408 ic_7408_1: pin names not known; wires that end beside it: op, op, comp, ic_7408_1_p4[14], ic_7404_1_p1, ic_7408_1_p6[14]
  assign xor_1_out = {15{ic_7408_1_p6[14]}} ^ B;  // XOR_Gate xor_1, 15 bits wide
  assign xor_2_out = {15{ic_7408_1_p4[14]}} ^ A;  // XOR_Gate xor_2, 15 bits wide
  Adder #(.width(15)) adder_1 (.a(xor_1_out), .b(xor_2_out), .out(out_5), .cin(op), .cout(cout));
endmodule
