// Logisim project ALU4.circ as structural Verilog: 1 circuit, main circuit ALU4
module ALU4 (
  input  [3:0] B,
  input  [3:0] A,
  output out_3,
  output comp,
  output [3:0] outp
);

  wire [3:0] not_1_out, xor_1_out, xor_2_out;

  Comparator #(.width(4), .mode("unsigned")) comparator_1 (.a(A), .b(B), .eq(out_3), .lt(comp));  // open: gt
  assign not_1_out = ~{4{comp}};  // NOT_Gate not_1, 4 bits wide
  assign xor_1_out = B ^ not_1_out;  // XOR_Gate xor_1, 4 bits wide
  assign xor_2_out = {4{comp}} ^ A;  // XOR_Gate xor_2, 4 bits wide
  Adder #(.width(4)) adder_1 (.a(xor_1_out), .b(xor_2_out), .out(outp), .cin(1'b1));  // open: cout
endmodule
