// Logisim project Normalizer.circ as structural Verilog: 1 circuit, main circuit Norm
module Norm (
  input  [14:0] min,
  input  op,
  input  [3:0] expin,
  input  cout,
  input  s0,
  output [14:0] mout,
  output zeros,
  output [3:0] expout,
  output undr
);

  wire multiplexer_5_out, or_1_out, sn_1_out_5;
  wire [3:0] an_1_exout, multiplexer_3_out, sn_1_exout;
  wire [14:0] an_1_mout, multiplexer_2_out, sn_1_mout;

  or or_1 (or_1_out, min[0], min[1], min[2], min[3], min[4], min[5], min[6], min[7], min[8], min[9], min[10], min[11], min[12], min[13], min[14]);
  AN an_1 (.cout(cout), .expin(expin), .min(min), .s0(s0), .mout(an_1_mout), .exout(an_1_exout));
  Multiplexer #(.width(15), .enable("false")) multiplexer_1 (
    .in0(multiplexer_2_out), .in1(min), .out(mout), .sel(zeros));
  not not_1 (zeros, or_1_out);
  SN sn_1 (.min(min), .expin(expin), .out_5(sn_1_out_5), .mout(sn_1_mout), .exout(sn_1_exout));
  and and_1 (undr, op, multiplexer_5_out);
  Multiplexer #(.width(15), .enable("false")) multiplexer_2 (
    .in0(an_1_mout), .in1(sn_1_mout), .out(multiplexer_2_out), .sel(op));
  Multiplexer #(.width(4), .enable("false")) multiplexer_3 (
    .in0(an_1_exout), .in1(sn_1_exout), .out(multiplexer_3_out), .sel(op));
  Multiplexer #(.width(4), .enable("false")) multiplexer_4 (
    .in0(multiplexer_3_out), .in1(4'b0000), .out(expout), .sel(zeros));
  Multiplexer #(.enable("false")) multiplexer_5 (.in0(sn_1_out_5), .in1(1'b0), .out(multiplexer_5_out), .sel(zeros));
endmodule
