// Logisim project addNormalizer.circ as structural Verilog: 1 circuit, main circuit AN
module AN (
  input  cout,
  input  [3:0] expin,
  input  [14:0] min,
  input  s0,
  output [14:0] mout,
  output [3:0] exout
);

  wire and_1_out;
  wire [14:0] shifter_1_out;

  Adder #(.width(4)) adder_1 (.a(expin), .b(4'b0000), .out(exout), .cin(cout));  // open: cout
  and and_1 (and_1_out, cout, min[0]);
  Shifter #(.width(15), .shift("lr")) shifter_1 (
    .in(min), .\dist ({3'b000, cout}), .out({shifter_1_out[14], mout[13:1], shifter_1_out[0]}));
  or or_1 (mout[0], and_1_out, s0);
  Multiplexer #(.enable("false")) multiplexer_1 (.in0(shifter_1_out[14]), .in1(1'b1), .out(mout[14]), .sel(cout));
endmodule
