// Logisim project checker.circ as structural Verilog: 1 circuit, main circuit CHK
module CHK (
  input  [3:0] expin,
  input  [10:0] min,
  output NaN,
  output INF,
  output DNM,
  output zero
);

  wire and_1_out, not_1_out, not_2_out, or_1_out, or_2_out;

  or or_1 (or_1_out, expin[0], expin[1], expin[2], expin[3]);
  and and_1 (and_1_out, expin[0], expin[1], expin[2], expin[3]);
  or or_2 (or_2_out, min[0], min[1], min[2], min[3], min[4], min[5], min[6], min[7], min[8], min[9], min[10]);
  not not_1 (not_1_out, or_1_out);
  not not_2 (not_2_out, or_2_out);
  and and_2 (DNM, not_1_out, or_2_out);
  and and_3 (zero, not_1_out, not_2_out);
  and and_4 (NaN, or_2_out, and_1_out);
  and and_5 (INF, and_1_out, not_2_out);
endmodule
