// Logisim project fpa.circ as structural Verilog: 1 circuit, main circuit main
module main (
  input  in_1,
  input  in_2,
  input  [14:0] in_3,
  input  [14:0] in_4,
  output [15:0] out_5
);

  wire alu4_1_comp, alu4_1_out_3, alu15_1_comp, alu15_1_cout, norm_1_zeros, not_1_out, rnd_1_norm,
       sgn_1_sign, shft_1_stk, xor_1_out;
  wire [3:0] alu4_1_outp, multiplexer_1_out, norm_1_expout;
  wire [14:0] alu15_1_out_5, an_1_mout, multiplexer_2_out, multiplexer_3_out, norm_1_mout, rnd_1_mout,
       shft_1_mout;

  xor xor_1 (xor_1_out, in_1, in_2);
  Multiplexer #(.width(4), .enable("false")) multiplexer_1 (
    .in0(in_3[14:11]), .in1(in_4[14:11]), .out(multiplexer_1_out), .sel(alu4_1_comp));
  ALU15 alu15_1 (
    .B(multiplexer_3_out), .A(shft_1_mout), .op(xor_1_out), .cout(alu15_1_cout), .comp(alu15_1_comp),
    .out_5(alu15_1_out_5));
  SGN sgn_1 (
    .sign(sgn_1_sign), .A(in_1), .comp(alu4_1_comp), .eq(alu4_1_out_3), .comp2(alu15_1_comp), .B(in_2),
    .op(xor_1_out));
  ALU4 alu4_1 (.B(in_4[14:11]), .A(in_3[14:11]), .out_3(alu4_1_out_3), .comp(alu4_1_comp), .outp(alu4_1_outp));
  SHFT shft_1 (.shift(alu4_1_outp), .min(multiplexer_2_out), .stk(shft_1_stk), .mout(shft_1_mout));
  Multiplexer #(.width(15), .enable("false")) multiplexer_2 (
    .in0({1'b1, in_4[10:0], 3'b000}), .in1({1'b1, in_3[10:0], 3'b000}), .out(multiplexer_2_out),
    .sel(alu4_1_comp));
  Multiplexer #(.width(15), .enable("false")) multiplexer_3 (
    .in0({1'b1, in_3[10:0], 3'b000}), .in1({1'b1, in_4[10:0], 3'b000}), .out(multiplexer_3_out),
    .sel(alu4_1_comp));
  Norm norm_1 (
    .min(alu15_1_out_5), .expin(multiplexer_1_out), .cout(alu15_1_cout), .s0(shft_1_stk), .op(xor_1_out),
    .mout(norm_1_mout), .zeros(norm_1_zeros), .expout(norm_1_expout));
  not not_1 (not_1_out, norm_1_zeros);
  RND rnd_1 (.min(norm_1_mout), .mout(rnd_1_mout), .norm(rnd_1_norm));
  and and_1 (out_5[15], not_1_out, sgn_1_sign);
  AN an_1 (
    .cout(rnd_1_norm), .expin(norm_1_expout), .min(rnd_1_mout), .s0(shft_1_stk),
    .mout({an_1_mout[14], out_5[10:0], an_1_mout[2:0]}), .exout(out_5[14:11]));
endmodule
