// Logisim project fpadder.circ as structural Verilog: 1 circuit, main circuit main
module main (
  input  [14:0] in_1,
  input  [14:0] in_2,
  input  in_3,
  input  in_4,
  output ovr,
  output undr,
  output [15:0] out_7,
  output Z,
  output D,
  output NaN,
  output INF,
  output [14:0] out_12,
  output [3:0] out_13
);

  wire alu4_1_comp, alu4_1_out_3, alu15_1_comp, alu15_1_cout, chk_1_dnm, chk_1_inf, chk_1_nan, chk_2_dnm,
       chk_2_inf, chk_2_nan, chk_3_dnm, chk_3_zero, nor_1_out, norm_1_zeros, not_1_out, rnd_1_norm,
       sgn_1_sign, shft_1_stk, xor_1_out;
  wire [3:0] alu4_1_outp, norm_1_expout;
  wire [14:0] alu15_1_out_5, an_1_mout, multiplexer_2_out, multiplexer_3_out, norm_1_mout, rnd_1_mout,
       shft_1_mout;
  wire [14:14] not_2_out, not_3_out;

  xor xor_1 (xor_1_out, in_3, in_4);
  Multiplexer #(.width(4), .enable("false")) multiplexer_1 (
    .in0(in_1[14:11]), .in1(in_2[14:11]), .out(out_13), .sel(alu4_1_comp));
  ALU15 alu15_1 (
    .B(multiplexer_3_out), .A(shft_1_mout), .op(xor_1_out), .cout(alu15_1_cout), .comp(alu15_1_comp),
    .out_5(alu15_1_out_5));
  SGN sgn_1 (
    .sign(sgn_1_sign), .A(in_3), .comp(alu4_1_comp), .eq(alu4_1_out_3), .comp2(alu15_1_comp), .B(in_4),
    .op(xor_1_out));
  ALU4 alu4_1 (.B(in_2[14:11]), .A(in_1[14:11]), .out_3(alu4_1_out_3), .comp(alu4_1_comp), .outp(alu4_1_outp));
  SHFT shft_1 (.shift(alu4_1_outp), .min(multiplexer_2_out), .stk(shft_1_stk), .mout(shft_1_mout));
  Multiplexer #(.width(15), .enable("false")) multiplexer_2 (
    .in0({not_3_out[14], in_2[10:0], 3'b000}), .in1({not_2_out[14], in_1[10:0], 3'b000}),
    .out(multiplexer_2_out), .sel(alu4_1_comp));
  Multiplexer #(.width(15), .enable("false")) multiplexer_3 (
    .in0({not_2_out[14], in_1[10:0], 3'b000}), .in1({not_3_out[14], in_2[10:0], 3'b000}),
    .out(multiplexer_3_out), .sel(alu4_1_comp));
  Norm norm_1 (
    .min(alu15_1_out_5), .expin(out_13), .cout(alu15_1_cout), .s0(shft_1_stk), .op(xor_1_out), .undr(undr),
    .mout(norm_1_mout), .zeros(norm_1_zeros), .expout(norm_1_expout));
  not not_1 (not_1_out, norm_1_zeros);
  RND rnd_1 (.min(norm_1_mout), .mout(rnd_1_mout), .norm(rnd_1_norm));
  and and_1 (out_7[15], not_1_out, sgn_1_sign);
  not not_2 (not_2_out[14], chk_1_dnm);
  AN an_1 (
    .cout(rnd_1_norm), .expin(norm_1_expout), .min(rnd_1_mout), .s0(shft_1_stk),
    .mout({an_1_mout[14], out_7[10:0], an_1_mout[2:0]}), .exout(out_7[14:11]));
  VLD vld_1 (
    .op(xor_1_out), .inf1(chk_1_inf), .nan1(chk_1_nan), .inf2(chk_2_inf), .nan2(chk_2_nan), .nano(NaN),
    .info(INF));
  CHK chk_1 (.expin(in_1[14:11]), .min(in_1[10:0]), .NaN(chk_1_nan), .INF(chk_1_inf), .DNM(chk_1_dnm));  // open: zero
  CHK chk_2 (.expin(in_2[14:11]), .min(in_2[10:0]), .NaN(chk_2_nan), .INF(chk_2_inf), .DNM(chk_2_dnm));  // open: zero
  not not_3 (not_3_out[14], chk_2_dnm);
  CHK chk_3 (.expin(out_7[14:11]), .min(out_7[10:0]), .DNM(chk_3_dnm), .zero(chk_3_zero));  // open: NaN, INF
  and and_2 (Z, chk_3_zero, nor_1_out);
  and and_3 (D, nor_1_out, chk_3_dnm);
  nor nor_1 (nor_1_out, INF, NaN);
  OVF ovf_1 (.en(nor_1_out), .expin(out_7[14:11]), .ovf(ovr));
endmodule
