// Logisim project overflow.circ as structural Verilog: 1 circuit, main circuit OVF
module OVF (
  input  en,
  input  [3:0] expin,
  output ovf
);

  and and_1 (ovf, expin[0], expin[1], expin[2], expin[3], en);
endmodule
