// Logisim project rounder.circ as structural Verilog: 1 circuit, main circuit RND
module RND (
  input  [14:0] min,
  output [14:0] mout,
  output norm
);

  wire or_1_out;
  wire [3:3] and_1_out;

  or or_1 (or_1_out, min[0], min[1], min[3]);
  and and_1 (and_1_out[3], or_1_out, min[2]);
  Adder #(.width(15)) adder_1 (
    .a({min[14:3], 3'b000}), .b({{11{1'b0}}, and_1_out[3], 3'b000}), .out(mout), .cin(1'b0), .cout(norm));
endmodule
