// Logisim project shifter.circ as structural Verilog: 1 circuit, main circuit SHFT
module SHFT (
  input  [14:0] min,
  input  [3:0] shift,
  output stk,
  output [14:0] mout
);

  wire [3:0] subtractor_1_out;
  wire [11:2] shifter_2_out;

  STK stk_1 (.shift(shift), .min(min[14:3]), .S(mout[0]));
  Shifter #(.width(12), .shift("lr")) shifter_1 (.in(min[14:3]), .\dist (shift), .out(mout[14:3]));
  Subtractor #(.width(4)) subtractor_1 (.a(shift), .b(4'b0010), .out(subtractor_1_out), .bin(1'b0));  // open: bout
  Shifter #(.width(12), .shift("lr")) shifter_2 (
    .in(min[14:3]), .\dist (subtractor_1_out), .out({shifter_2_out, mout[2:1]}));

  assign stk = mout[0];
endmodule
