// Logisim project signer.circ as structural Verilog: 1 circuit, main circuit SGN
module SGN (
  input  comp,
  input  eq,
  input  comp2,
  input  B,
  input  A,
  input  op,
  output sign
);

  wire and_1_out, multiplexer_2_out, or_1_out;

  and and_1 (and_1_out, comp2, eq);
  Multiplexer #(.enable("false")) multiplexer_1 (.in0(A), .in1(multiplexer_2_out), .out(sign), .sel(op));
  or or_1 (or_1_out, and_1_out, comp);
  Multiplexer #(.enable("false")) multiplexer_2 (.in0(A), .in1(B), .out(multiplexer_2_out), .sel(or_1_out));
endmodule
