// Logisim project sticky.circ as structural Verilog: 1 circuit, main circuit STK
module STK (
  input  [11:0] min,
  input  [3:0] shift,
  output S
);

  wire or_1_out, or_2_out;
  wire [3:0] subtractor_1_out;
  wire [11:0] and_1_out, decoder_1_out0, subtractor_2_out;

  or or_1 (or_1_out, shift[1], shift[2], shift[3]);
  Subtractor #(.width(4)) subtractor_1 (.a(shift), .b(4'b0010), .out(subtractor_1_out), .bin(1'b0));  // open: bout
  Decoder #(.select(4), .enable("false")) decoder_1 (
    .out0(decoder_1_out0[0]), .out1(decoder_1_out0[1]), .out2(decoder_1_out0[2]), .out3(decoder_1_out0[3]),
    .out4(decoder_1_out0[4]), .out5(decoder_1_out0[5]), .out6(decoder_1_out0[6]), .out7(decoder_1_out0[7]),
    .out8(decoder_1_out0[8]), .out9(decoder_1_out0[9]), .out10(decoder_1_out0[10]),
    .out11(decoder_1_out0[11]), .sel(subtractor_1_out));  // open: out12, out13, out14, out15
  Multiplexer #(.enable("false")) multiplexer_1 (.in0(1'b0), .in1(or_2_out), .out(S), .sel(or_1_out));
  or or_2 (or_2_out, and_1_out[0], and_1_out[1], and_1_out[2], and_1_out[3], and_1_out[4], and_1_out[5], and_1_out[7], and_1_out[8], and_1_out[9], and_1_out[10], and_1_out[11], and_1_out[6]);
  Subtractor #(.width(12)) subtractor_2 (
    .a(decoder_1_out0), .b({12{1'b0}}), .out(subtractor_2_out), .bin(1'b1));  // open: bout
  assign and_1_out = subtractor_2_out & min;  // AND_Gate and_1, 12 bits wide
endmodule
