// Logisim project subNormalizer.circ as structural Verilog: 1 circuit, main circuit SN
module SN (
  input  [14:0] min,
  input  [3:0] expin,
  output [14:0] mout,
  output [3:0] exout,
  output out_5
);

  wire [3:0] priority_encoder_1_out, subtractor_1_out, subtractor_2_out;

  Priority_Encoder #(.select(4)) priority_encoder_1 (
    .in0(min[0]), .in1(min[1]), .in2(min[2]), .in3(min[3]), .in4(min[4]), .in5(min[5]), .in6(min[6]),
    .in7(min[7]), .in8(min[8]), .in9(min[9]), .in10(min[10]), .in11(min[11]), .in12(min[12]), .in13(min[13]),
    .in14(min[14]), .in15(1'b0), .out(priority_encoder_1_out), .en_in(1'b1));  // open: gs, en_out
  Subtractor #(.width(4)) subtractor_1 (
    .a(4'b1110), .b(priority_encoder_1_out), .out(subtractor_1_out), .bin(1'b0));  // open: bout
  Shifter #(.width(15)) shifter_1 (.in(min), .\dist (subtractor_1_out), .out(mout));
  Subtractor #(.width(4)) subtractor_2 (
    .a(expin), .b(subtractor_1_out), .out(subtractor_2_out), .bin(1'b0));  // open: bout
  Comparator #(.width(4), .mode("unsigned")) comparator_1 (
    .a(subtractor_1_out), .b(expin), .gt(out_5));  // open: eq, lt
  Multiplexer #(.width(4), .enable("false")) multiplexer_1 (
    .in0(subtractor_2_out), .in1(4'b0000), .out(exout), .sel(out_5));
endmodule
