// Logisim project validator.circ as structural Verilog: 1 circuit, main circuit VLD
module VLD (
  input  op,
  input  inf1,
  input  nan1,
  input  inf2,
  input  nan2,
  output nano,
  output info
);

  wire and_1_out, and_2_out, and_3_out, not_1_out, not_2_out, or_1_out, or_2_out, xor_1_out;

  not not_1 (not_1_out, op);
  xor xor_1 (xor_1_out, inf2, inf1);
  and and_1 (and_1_out, inf1, inf2);
  and and_2 (and_2_out, and_1_out, op);
  and and_3 (and_3_out, and_1_out, not_1_out);
  or or_1 (or_1_out, nan2, nan1);
  or or_2 (or_2_out, and_3_out, xor_1_out);
  or or_3 (nano, or_1_out, and_2_out);
  not not_2 (not_2_out, nano);
  and and_4 (info, not_2_out, or_2_out);
endmodule
